# Fritzing sketch Robot-Elektrisch-Schema (saved by Fritzing 0.8.7b)
stripboards: 1

parts:
  Part1 = Arduino Uno (Rev3)
  M1 = DC Motor
  M2 = DC Motor
  M3 = DC Motor  # not connected
  M4 = DC Motor  # not connected
  M5 = DC Motor

nets:
  N1: Part1.D12/MISO, M1.pin_2
  N2: Part1.D13/SCK, M2.pin_2
  N3: Part1.D2, M5.pin_2
  N4: Part1.GND, M1.pin_1, M2.pin_1, M5.pin_1

notes:
  Ultrasonic Front
  Ultrasonic Side
  Compass
  Motor Driver
  Brushes
  Pump
  Motors
